// Digital circuit circuit_D0.dig as structural Verilog
module circuit_D0 (
  input  X1,
  input  X1_2,
  input  X0,
  input  X0_2,
  input  Q2,
  input  Q2_2,
  input  Q1,
  input  Q0,
  output D0
);

  wire or_1_out, or_2_out, or_3_out;

  or or_1 (or_1_out, Q2, Q0, X1, X0);
  or or_2 (or_2_out, Q2, Q1, X1, X0_2);
  or or_3 (or_3_out, Q2_2, Q0, X1_2);
  and and_1 (D0, or_1_out, or_2_out, or_3_out);
endmodule
