// Digital circuit circuit_D2.dig as structural Verilog
module circuit_D2 (
  input  X1,
  input  X0,
  input  X0_2,
  input  Q2,
  input  Q1,
  input  Q0,
  input  Q0_2,
  output D2
);

  wire and_1_out, and_2_out, and_3_out, and_4_out;

  and and_1 (and_1_out, Q2, Q1, Q0, X0_2);
  and and_2 (and_2_out, Q2, Q1, Q0_2, X0);
  and and_3 (and_3_out, Q2, X1);
  and and_4 (and_4_out, Q0_2, X1);
  or or_1 (D2, and_1_out, and_2_out, and_3_out, and_4_out);
endmodule
