// Digital circuit circuit_G.dig as structural Verilog
module circuit_G (
  input  Q2,
  input  Q1,
  input  Q0,
  output G
);

  wire and_1_out, and_2_out;

  and and_1 (and_1_out, Q2, Q0);
  and and_2 (and_2_out, Q1, Q0);
  or or_1 (G, and_1_out, and_2_out);
endmodule
