// Digital circuit circuit_R.dig as structural Verilog
module circuit_R (
  input  Q2,
  input  Q1,
  input  Q0,
  input  Q0_2,
  output R
);

  wire and_1_out, and_2_out;

  and and_1 (and_1_out, Q2, Q0);
  and and_2 (and_2_out, Q1, Q0_2);
  or or_1 (R, and_1_out, and_2_out);
endmodule
