// Digital circuit solucio.dig as structural Verilog
module solucio (
  input  X1,
  input  X0,
  input  clk,
  output BLAU,
  output GROC,
  output VERMELL,
  output VERD
);

  wire circuit_d0_1_d0, circuit_d1_1_d1, circuit_d2_1_d2, d_ff_1_nq, d_ff_1_q, d_ff_2_nq, d_ff_2_q,
       d_ff_3_nq, not_1_out, not_2_out;

  not not_1 (not_1_out, X1);
  not not_2 (not_2_out, X0);
  circuit_D0 circuit_d0_1 (
    .X1(X1), .X1_2(not_1_out), .X0(X0), .X0_2(not_2_out), .Q2(BLAU), .Q2_2(d_ff_3_nq), .Q1(d_ff_2_nq),
    .Q0(d_ff_1_nq), .D0(circuit_d0_1_d0));
  circuit_D1 circuit_d1_1 (
    .X1(not_1_out), .X0(X0), .X0_2(not_2_out), .Q2(d_ff_3_nq), .Q1(d_ff_2_q), .Q1_2(d_ff_2_nq),
    .Q0(d_ff_1_q), .Q0_2(d_ff_1_nq), .D1(circuit_d1_1_d1));
  circuit_D2 circuit_d2_1 (
    .X1(X1), .X0(X0), .X0_2(not_2_out), .Q2(d_ff_3_nq), .Q1(d_ff_2_q), .Q0(d_ff_1_q), .Q0_2(d_ff_1_nq),
    .D2(circuit_d2_1_d2));
  D_FF d_ff_1 (.D(circuit_d0_1_d0), .C(clk), .Q(d_ff_1_q), .nQ(d_ff_1_nq));
  D_FF d_ff_2 (.D(circuit_d1_1_d1), .C(clk), .Q(d_ff_2_q), .nQ(d_ff_2_nq));
  D_FF d_ff_3 (.D(circuit_d2_1_d2), .C(clk), .Q(BLAU), .nQ(d_ff_3_nq));
  circuit_V circuit_v_1 (.Q1(d_ff_2_nq), .Q0(d_ff_1_q), .V(VERD));
  circuit_R circuit_r_1 (.Q2(BLAU), .Q1(d_ff_2_q), .Q0(d_ff_1_q), .Q0_2(d_ff_1_nq), .R(VERMELL));
  circuit_G circuit_g_1 (.Q2(BLAU), .Q1(d_ff_2_q), .Q0(d_ff_1_q), .G(GROC));
  LED LED_VERD (.in(VERD));
  LED LED_VERMELL (.in(VERMELL));
  LED LED_GROC (.in(GROC));
  LED LED_BLAU (.in(BLAU));

  // Notes on the sheet:
  //   Q1'
  //   Q1
  //   Q2'
  //   Q2
  //   Q0'
  //   Q0
  //   D0
  //   D1
  //   D2
endmodule
